# Fritzing sketch shutter-timer-circuit (saved by Fritzing 0.9.3b)
breadboards: 1

parts:
  U1 = 555 Timer [package="DIP8 [THT]"]
  U2 = POT [package=pot_mammoth]
  Q1 = LTR-301 [package=ltr-301]
  Uno = Arduino Uno (Rev3)
  speaker = Piezo Speaker
  C1 = Ceramic Capacitor [capacitance=100nF package="100 mil [THT, multilayer]"]

nets:
  N1: U1.Ground, U2.A, Uno.GND, speaker.pin2, C1.0
  N2: U1.Trigger, U1.Threshold, U2.E, Q1.E
  N3: U1.Output, Uno.D7
  N4: U1.Reset, U1.Vcc_Supply_Voltage, Q1.C, Uno.5V
  N5: Uno.D10_PWM/SS, speaker.pin1
